# Fritzing sketch robot (saved by Fritzing 0.9.3b)
breadboards: 1

parts:
  R1 = Photocell (LDR) [package=THT]
  VCC1 = Battery block 9V
  Motor_A = DC Motor
  Motor_B = DC Motor
  R4 = Photocell (LDR) [package=THT]
  LED2 = LED - 5mm [color="Infrared (940nm)" package="5 mm [THT]"]
  R6 = Resistor [tolerance=±5% resistance=10k package=THT]
  LED1 = LED - 3mm [color="Infrared (940nm)" package="3 mm [THT]"]
  Part3 = Motor Driver 1A Dual TB6612FNG
  R8 = Resistor [tolerance=±5% resistance=10k package=THT]
  R9 = Resistor [tolerance=±5% resistance=330 package=THT]
  D1 = Rectifier Diode [part_number=1N4001 package="300 mil [THT]"]
  R10 = Resistor [tolerance=±5% resistance=56 package=THT]
  Part4 = Arduino Uno (Rev3)
  L2 = Solenoid
  Q1 = NPN-Transistor [package="SOT-23 [SMD]"]
  L1 = Solenoid

nets:
  N1: R1.pin_0, R8.Pin_0, Part4.D2
  GND: R1.pin_1, VCC1.-, R4.pin_1, Part3.GND, R10.Pin_1, Part4.GND, Q1.2
  N2: VCC1.+, Part3.VM, D1.cathode, Part4.VIN, L2.pin2, L1.pin2
  N3: Motor_A.pin_1, Part3.A01
  N4: Motor_A.pin_2, Part3.A02
  N5: Motor_B.pin_1, Part3.B02
  N6: Motor_B.pin_2, Part3.B01
  N7: R4.pin_0, R6.Pin_0, Part4.D3_PWM
  N8: LED2.cathode, LED1.cathode, R10.Pin_0
  VCC: LED2.anode, R6.Pin_1, LED1.anode, Part3.VCC, R8.Pin_1, Part4.5V
  N9: Part3.PWMA, Part4.D5_PWM
  N10: Part3.AIN2, Part4.D4
  N11: Part3.AIN1, Part4.D11_PWM/MOSI
  N12: Part3.STBY, Part4.D9_PWM
  N13: Part3.BIN1, Part4.D7
  N14: Part3.BIN2, Part4.D8
  N15: Part3.PWMB, Part4.D6_PWM
  N16: R9.Pin_0, Part4.D10_PWM/SS
  N17: R9.Pin_1, Q1.0
  N18: D1.anode, L2.pin1, Q1.1, L1.pin1

custom parts:
  Motor Driver 1A Dual TB6612FNG: The TB6612FNG motor driver can control up to two DC motors at a constant current of 1.2A (3.2A peak). Two input signals (IN1 and IN2) can be used to control the motor in one of four function modes - CW, CCW, short-brake, and stop. The two motor outputs (A and B) can be separately controlled, the speed of each motor is controlled via a PWM input signal with a frequency up to 100kHz. The STBY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

// code stored in the sketch: SOEV.ino
//<define the IO pins for easier Refrencce>
//2=A,3=B
// #define is good for IO pins because #define and IO pins are both hard wiring
#define brkpin 10
#define tachpin 3
//</define the IO pins for easier Refrencce>
#define wedge 4.14 //distance around wheel between inturrupts, ~4.14cm, 

//<Init Motor Drivers>
// Creadit where cedit is due - This was copied and pasted from the Sparkfun Hookup Guide
//https://github.com/sparkfun/SparkFun_TB6612FNG_Arduino_Library/blob/master/examples/MotorTestRun/MotorTestRun.ino11
// This is the library for the TB6612 that contains the class Motor and all the
// functions
#include <SparkFun_TB6612.h>

// Pins for all inputs, keep in mind the PWM defines must be on PWM pins
// the default pins listed are the ones used on the Redbot (ROB-12097) with
// the exception of STBY which the Redbot controls with a physical switch
#define AIN1 11
#define BIN1 7
#define AIN2 4
#define BIN2 8
#define PWMA 5
#define PWMB 6
#define STBY 9

// Initializing motors.  The library will allow you to initialize as many
// motors as you have memory for.  If you are using functions like forward
// that take 2 motors as arguements you can either write new functions or
// call the function more than once.
Motor A = Motor(AIN1, AIN2, PWMA, 1, STBY);//this runs forwards
Motor B = Motor(BIN1, BIN2, PWMB, -1, STBY);//this runs backwards
//</Init Motor Drivers>

//<Init Variables>
//Floats are evil due to slow computation speeds. AVOID!
unsigned long trk = 1000; //use cm
volatile float loc; //use cm
const unsigned long decel = 1; //use cm*(cm/ms)
unsigned long spd; //speed in cm/ms
//<used by tachometer>
//global becuase they are used in tachLog() and tachCount()
volatile unsigned long lastTach2;
volatile unsigned long thisTach2;
volatile unsigned long lastTach3;
volatile unsigned long thisTach3;
//<used by tachCount Function>
//<Speed used by motors>
byte Aspd = 255; //Start Motor A @ 255
byte Bspd = 255; //Start Motor B @ 255
//<speed used by motors>
//<used by tachcount, global for efficiency>
unsigned long lclLast;
unsigned long lclThis;
unsigned long spd2;
unsigned long spd3;
//</used by tachcount, global for efficiency>
const int PHOTO_PIN_1 = A0;
const int LEDS_PIN = 2;
//</Init Variables>
// Number of samples to take for calibration
const int CALIBRATION_SAMPLES = 20;

int threshold_1;
int threshold_2;


void setup() {
  pinMode(LEDS_PIN, OUTPUT);
  unsigned int avg_lit_1 = 0;
  unsigned int avg_unlit_1 = 0;
  int i;

  // Set pins for output LEDs
  pinMode(LEDS_PIN, OUTPUT);

  // Turn on LEDs and wait a few ms for them to be fully on
  digitalWrite(LEDS_PIN, HIGH);
  delay(100);

  // Find average light value for sensors with LEDs on
  for ( i = 0; i < CALIBRATION_SAMPLES; i++ ) {
    avg_lit_1 += analogRead(PHOTO_PIN_1);
  }
  avg_lit_1 /= CALIBRATION_SAMPLES;

  // Turn off LEDs and wait a few ms for them to be fully off
  digitalWrite(LEDS_PIN, LOW);
  delay(100);

  // Find average light value for sensors with LEDs off
  for ( i = 0; i < CALIBRATION_SAMPLES; i++ ) {
    avg_unlit_1 += analogRead(PHOTO_PIN_1);
  }
  avg_unlit_1 /= CALIBRATION_SAMPLES;

  // Calculate thresholds (half way between lit and unlit values)
  threshold_1 = ((avg_lit_1 - avg_unlit_1) / 2) + avg_unlit_1;

  // Turn on output LEDs and wait for them to be fully on
  digitalWrite(LEDS_PIN, HIGH);
  delay(100);


  Serial.begin(9600);//Start Serial
  /*//<pull tracklength from serial>
    long sertrk = 0; //a var to hold parseint
    while (sertrk = 0) {//wait to recieve the value from the port
    sertrk = Serial.parseInt();//pass the value into a local variable
    }
    trk = sertrk; //set serial to the value pulled from the port
    //</pull tracklength from serial>*/
  //<turn on LED 13 to signify init>
  pinMode(13, OUTPUT);
  digitalWrite(13, HIGH);
  //</turn on LED 13 to signify init>
  //<pin Modes>
  pinMode(brkpin, OUTPUT);
  pinMode(tachpin, INPUT);
  //</pin Modes>
  A.drive(Aspd); //turn the motor on
  B.drive(Bspd); //turn the motor on
  Serial.println("loc,spd,lastTach2,thisTach2,lastTach3,thisTach3,Aspd,Bspd"); //tells the order of the variables when printed
  digitalWrite(13, LOW);
}

void loop() {
  Serial.println(analogRead(PHOTO_PIN_1));
  int photo_light_1;
  int photo_light_2;
  unsigned long time_1;

  // Read light from sensors
  photo_light_1 = analogRead(PHOTO_PIN_1);

  // See if object passed in front of sensor 1
  if ( photo_light_1 <= threshold_1 ) {
    loc += wedge;
  }
  //<Do this every time the code runs>
  /*<log all the variables for debuging>
    Serial.print(loc);
    Serial.print(",");
    Serial.print(spd);
    Serial.print(",");
    Serial.print(lastTach2);
    Serial.print(",");
    Serial.print(thisTach2);
    Serial.print(",");
    Serial.print(lastTach3);
    Serial.print(",");
    Serial.print(thisTach3);
    Serial.print(",");
    Serial.print(Aspd);
    Serial.print(",");
    Serial.println(Bspd);
    //</log all the variable for debugging>*/
  //</Do this every time the code runs>
  //<Only if we are stopping>
  if (loc >= trk) { //if we are running out of track //SHOULD BE trk - loc <= decel * spd
    Serial.print("Break");
    A.brake(); //brake the motors
    B.brake(); //brake the motors
    digitalWrite(brkpin, HIGH); //fire the solenoids
    //</Only if we are stopping>
  } else { //<if there is track left>
    /*//<set the motor Speeds>
      if (spd2 > spd3) {//if motor A is going faster
      Aspd--;//slow it down
      } else if (spd2 < spd3) { //guess
      Bspd--;//Just guess
      }//I hope you cant miss
      //here it gets interesting
      //<make sure the motors are a full speed>
      if (Aspd <= Bspd && Bspd < 255) { //if Bspeed is the highest one, and there is room to raise it
      Aspd += 255 - Bspd; //increase Aspd by the difference between Bspd and the maximum possible value
      Bspd += 255 - Bspd; //Look up, and guess
      } else if (Bspd <= Aspd && Aspd < 255) { ///if Aspeed is the highest one, and there is room to raise it
      Aspd += 255 - Aspd; //increase ABspd by the difference between Bspd and the maximum possible value
      Bspd += 255 - Aspd; //There is one difference, do you see it?
      }
      //</make sure the motors are a full speed>
      //</Set the motor Speeds>*/
    A.drive(Aspd); //turn the motor on
    B.drive(Bspd); //turn the motor on
  }
  //</if there is track left>
  Serial.println("loop");
}

void tachCount2() {
  //<local variables>
  //I use local variables so that if tachcount is called in the middle of the function it wont make the maths go poof.
  lclLast = lastTach2;
  lclThis = thisTach2;
  //</local Variables>
  spd2 = wedge / (lclThis - lclLast) * 100; //cm/ms, //wedge = dist, //* 100 is to avoid floating point stuff
  /*if (!(lclThis == thisTach2)) {//if tachLog1 has been called since we started
    tachCount2();//do this function again
    //I love recursion
    }*/
}

void tachCount3() {
  //<local variables>
  //I use local variables so that if tachcount is called in the middle of the function it wont make the maths go poof.
  lclLast = lastTach3;
  lclThis = thisTach3;
  //</local Variables>
  spd3 = wedge / (lclThis - lclLast) * 100; //cm/ms, //wedge = dist, //* 100 is to avoid floating point stuff
  /*if (!(lclThis == thisTach2)) {//if tachLog1 has been called since we started
    tachCount3();//do this function again
    //I love recursion
    }*/
}
